# Fritzing sketch Beethduino_Fritzing_sketch (saved by Fritzing 0.6.3b)
breadboards: 1

parts:
  Arduino1 = Arduino
  LCD1 = LCD screen
  R1 = Rotary Potentiometer (Small) [maximum_resistance=100kΩ]
  S1 = Pushbutton [package="[THT]"]
  S2 = Pushbutton [package="[THT]"]
  S3 = Pushbutton [package="[THT]"]
  S4 = Pushbutton [package="[THT]"]
  S5 = Pushbutton [package="[THT]"]
  R2 = Resistor [tolerance=±5% resistance=10k package=THT]
  R3 = Resistor [tolerance=±5% resistance=10k package=THT]
  R4 = Resistor [tolerance=±5% resistance=10k package=THT]
  R5 = Resistor [tolerance=±5% resistance=10k package=THT]
  R6 = Resistor [tolerance=±5% resistance=10k package=THT]
  J1 = Piezo Speaker

nets:
  GND: Arduino1.GND, LCD1.VSS, LCD1.R/W, LCD1.LED-, R1.leg2, R2.Pin_0, R3.Pin_0, R4.Pin_0, R5.Pin_0, R6.Pin_0, J1.pin1
  N1: Arduino1.D13, S1.Pin_3, S1.Pin_4, R2.Pin_1
  N2: Arduino1.D12, S5.Pin_3, S5.Pin_4, R3.Pin_1
  N3: Arduino1.D11, S4.Pin_3, S4.Pin_4, R4.Pin_1
  N4: Arduino1.D10, S2.Pin_3, S2.Pin_4, R6.Pin_1
  N5: Arduino1.D9, S3.Pin_3, S3.Pin_4, R5.Pin_1
  N6: Arduino1.D8, J1.pin2
  N7: Arduino1.D7, LCD1.DB7
  N8: Arduino1.D6, LCD1.DB6
  N9: Arduino1.D5, LCD1.DB5
  N10: Arduino1.D4, LCD1.DB4
  N11: Arduino1.D3, LCD1.E
  N12: Arduino1.D2, LCD1.RS
  N13: Arduino1.3V3, LCD1.LED+
  +5V: Arduino1.+5V, LCD1.VDD, R1.leg1, S1.Pin_1, S1.Pin_2, S2.Pin_1, S2.Pin_2, S3.Pin_1, S3.Pin_2, S4.Pin_1, S4.Pin_2, S5.Pin_1, S5.Pin_2
  N14: LCD1.V0, R1.wiper
